// Logisim project Simple CPU.circ as structural Verilog: 4 circuits, main circuit Simple CPU
// CPU
module Simple_CPU (
  input  [7:0] From_MBR,
  input  [7:0] B_In,
  input  Clock,
  input  Reset,
  output [7:0] To_MBR,
  output [7:0] Out,
  output [7:0] A_Reg_Debug,
  output [7:0] B_Reg_Debug
);

  wire PC_Reg;
  wire [1:0] BSel;
  wire [2:0] ALU_Control;
  wire [4:0] Reg_Write;
  wire [7:0] alu_1_c, From_MBR_t, multiplexer_1_out;

  Register register_1 (.D(alu_1_c), .Q(To_MBR), .clk(PC_Reg), .clr(Reset));  // open: en
  Register register_2 (.D(alu_1_c), .Q(Out), .clk(Reg_Write[4]), .clr(Reset));  // open: en
  Register register_3 (.D(alu_1_c), .Q(B_Reg_Debug), .clk(Reg_Write[1]), .clr(Reset));  // open: en
  Register register_4 (.D(alu_1_c), .Q(A_Reg_Debug), .clk(Reg_Write[0]), .clr(Reset));  // open: en
  Register register_5 (.D(From_MBR), .Q(From_MBR_t), .clk(Reg_Write[2]), .clr(Reset));  // open: en
  Multiplexer #(.select(2), .width(8), .enable("false")) multiplexer_1 (
    .in0(B_Reg_Debug), .in1(From_MBR_t), .in2(To_MBR), .in3(B_In), .out(multiplexer_1_out), .sel(BSel));
  ALU alu_1 (.A(A_Reg_Debug), .B(multiplexer_1_out), .C(alu_1_c), .F2_F1_F0(ALU_Control));
  Control_Unit control_unit_1 (
    .ALU_control(ALU_Control), .Register_write_control({Reg_Write[4], PC_Reg, Reg_Write[2:0]}),
    .ALU_B_Bus_Select(BSel), .From_MBR({1'b0, From_MBR_t[3:0]}), .Clock(Clock), .Reset(Reset));

  // Other names for the same wires on the sheet: A_Reg[7:0] = A_Reg_Debug; B_Reg[7:0] = B_Reg_Debug; R = Reset;
  //   Reg_Write[3] = PC_Reg

  // Notes on the sheet:
  //   PC
  //   Out
  //   B
  //   A
  //   MBR
  //   Debug
  //   Outputs
  //   Inputs
endmodule

module ALU (
  input  [7:0] A,
  input  [7:0] B,
  input  [2:0] F2_F1_F0,
  output [7:0] C
);

  wire [7:0] adder_1_out, adder_2_out, adder_3_out, and_1_out, or_1_out, subtractor_1_out;

  Adder adder_1 (.a(A), .b(8'h1), .out(adder_1_out));  // open: cin, cout
  Adder adder_2 (.a(B), .b(8'h1), .out(adder_2_out));  // open: cin, cout
  Adder adder_3 (.a(A), .b(B), .out(adder_3_out));  // open: cin, cout
  Subtractor subtractor_1 (.a(A), .b(B), .out(subtractor_1_out));  // open: bin, bout
  assign and_1_out = A & B;  // AND_Gate and_1, 8 bits wide
  assign or_1_out = A | B;  // OR_Gate or_1, 8 bits wide
  Multiplexer #(.select(3), .width(8), .enable("false")) multiplexer_1 (
    .in0(A), .in1(B), .in2(adder_1_out), .in3(adder_2_out), .in4(adder_3_out), .in5(subtractor_1_out),
    .in6(and_1_out), .in7(or_1_out), .out(C), .sel(F2_F1_F0));

  // Notes on the sheet:
  //   A
  //   B
  //   1
endmodule

module Control_Unit (
  input  [4:0] From_MBR,
  input  Clock,
  input  Reset,
  output [4:0] Register_write_control,
  output [1:0] ALU_B_Bus_Select,
  output [2:0] ALU_control
);

  wire JMPC;
  wire [4:0] MIR_q, MPC_q, multiplexer_1_out;
  wire [15:0] MIR;

  Multiplexer #(.width(5), .enable("false")) multiplexer_1 (
    .in0(MIR_q), .in1(From_MBR), .out(multiplexer_1_out), .sel(JMPC));
  Register #(.width(5)) MPC (.D(multiplexer_1_out), .Q(MPC_q), .clk(Clock), .clr(Reset));  // open: en
  ROM #(.addrWidth(5), .dataWidth(16)) rom_1 (.addr(MPC_q), .data(MIR));  // open: sel
  Register #(.width(16)) u_MIR (
    .D(MIR), .Q({MIR_q, JMPC, ALU_control, ALU_B_Bus_Select, Register_write_control}), .clk(Clock),
    .clr(Reset));  // open: en

  // Notes on the sheet:
  //   Microprogram Control Store
  //   contents of rom_1 (hex, n*v repeats v):
  //   e804 0 80e0 10 88a4 90a4 98a4 a100 a980 2 b080 ba00 c280 6800 cb00 d380 e1 a8 d8a1 d8a2 101 182 81
  //   201 281 301 381 e1c0 1c8 f1c0 f9c8 400
endmodule

module main (
  input  [7:0] in_1,
  input  Clear_RAM,
  input  Reset
);

  wire Clock_out;
  wire [7:0] A_Reg, B_Reg, ram_1_data, simple_cpu_1_out, simple_cpu_1_to_mbr;

  Hex_Digit_Display hex_digit_display_1 (.value(A_Reg[7:4]));  // open: dp
  Hex_Digit_Display hex_digit_display_2 (.value(A_Reg[3:0]));  // open: dp
  Hex_Digit_Display hex_digit_display_3 (.value(B_Reg[7:4]));  // open: dp
  Hex_Digit_Display hex_digit_display_4 (.value(B_Reg[3:0]));  // open: dp
  RAM ram_1 (.addr(simple_cpu_1_to_mbr), .data(ram_1_data), .clr(Clear_RAM));  // open: sel, clk, ld
  Simple_CPU simple_cpu_1 (
    .From_MBR(ram_1_data), .To_MBR(simple_cpu_1_to_mbr), .B_In(in_1), .Out(simple_cpu_1_out),
    .Clock(Clock_out), .Reset(Reset), .A_Reg_Debug(A_Reg), .B_Reg_Debug(B_Reg));
  Clock Clock (.out(Clock_out));
  Hex_Digit_Display hex_digit_display_5 (.value(simple_cpu_1_out[3:0]));  // open: dp
  Hex_Digit_Display hex_digit_display_6 (.value(simple_cpu_1_out[7:4]));  // open: dp

  // Notes on the sheet:
  //   DEBUG
  //   A
  //   B
  //   RAM
  //   OP CODES
  //   01 NOP
  //   02 INPUT
  //   03 OUTPUT
  //   04 JUMP
  //   05 LOAD A
  //   06 LOAD B
  //   07 INC A
  //   08 INC B
  //   0B ADD A,B
  //   0C SUB A,B
  //   0D HALT
  //   0F A OR B
  //   09 MOV B,A
  //   0A MOV A,B
  //   0E A AND B
endmodule
